// Logisim project cpu.circ as structural Verilog: 1 circuit, main circuit cpu
module cpu (
  input  clk,
  input  [31:0] INSTRUCTION,
  input  [31:0] MEM_READ_DATA,
  output [31:0] MEM_WRITE_ADDRESS,
  output [31:0] PROGRAM_COUNTER,
  output [31:0] ra,
  output [31:0] sp,
  output [31:0] t0,
  output [31:0] t1,
  output [31:0] t2,
  output [31:0] s0,
  output [31:0] s1,
  output [31:0] a0,
  output [31:0] tohost,
  output [3:0] MEM_WRITE_ENABLE,
  output [31:0] MEM_WRITE_DATA
);

  wire ASel, BrEq, BrLt, BrUn, BSel, CSRSel, CSRWen, MemRW, PCSel, RegWEn;
  wire [1:0] ALU_res, WBSel;
  wire [2:0] ImmSel;
  wire [3:0] ALUSel, multiplexer_6_out, multiplexer_10_out, multiplexer_12_out, shifter_5_out, shifter_6_out;
  wire [31:0] adder_1_out, and_1_out, bit_extender_1_out, bit_extender_2_out, bit_extender_3_out,
       bit_extender_4_out, bit_extender_5_out, bit_extender_6_out, imm_gen_1_imm, mem_data,
       multiplexer_1_out, multiplexer_2_out, multiplexer_3_out, multiplexer_4_out, multiplexer_5_out,
       multiplexer_7_out, multiplexer_8_out, multiplexer_9_out, multiplexer_11_out, regfile_1_read_data_1,
       rs2, shifter_1_out;

  Adder #(.width(32)) adder_1 (.a(PROGRAM_COUNTER), .b(32'h4), .out(adder_1_out));  // open: cin, cout
  Multiplexer #(.enable("false"), .width(32)) multiplexer_1 (
    .in0(adder_1_out), .in1({MEM_WRITE_ADDRESS[31:2], ALU_res}), .out(multiplexer_1_out), .sel(PCSel));
  Multiplexer #(.enable("false"), .width(32)) multiplexer_2 (
    .in0(regfile_1_read_data_1), .in1(imm_gen_1_imm), .out(multiplexer_2_out), .sel(CSRSel));
  Register #(.width(32)) PC (.D(multiplexer_1_out), .clk(clk), .Q(PROGRAM_COUNTER));  // open: en, clr
  regfile regfile_1 (
    .rs1(INSTRUCTION[19:15]), .rs2(INSTRUCTION[24:20]), .rd(INSTRUCTION[11:7]),
    .Write_Data(multiplexer_5_out), .RegWEn(RegWEn), .clk(clk), .ra(ra), .sp(sp), .t0(t0), .t1(t1), .t2(t2),
    .s0(s0), .s1(s1), .a0(a0), .Read_Data_1(regfile_1_read_data_1), .Read_Data_2(rs2));
  imm_gen imm_gen_1 (.inst(INSTRUCTION), .ImmSel(ImmSel), .imm(imm_gen_1_imm));
  // csr csr_1: pin names not known; wires that end beside it: INSTRUCTION[31:20], multiplexer_2_out, CSRWen, clk, tohost
  Multiplexer #(.enable("false"), .width(32)) multiplexer_3 (
    .in0(regfile_1_read_data_1), .in1(PROGRAM_COUNTER), .out(multiplexer_3_out), .sel(ASel));
  Multiplexer #(.enable("false"), .width(32)) multiplexer_4 (
    .in0(rs2), .in1(imm_gen_1_imm), .out(multiplexer_4_out), .sel(BSel));
  branch_comp branch_comp_1 (.rs1(regfile_1_read_data_1), .rs2(rs2), .BrUn(BrUn), .BrEq(BrEq), .BrLt(BrLt));
  control_logic control_logic_1 (
    .CSRWen(CSRWen), .PCSel(PCSel), .RegWEn(RegWEn), .ImmSel(ImmSel), .BrUn(BrUn), .ASel(ASel), .BSel(BSel),
    .ALUSel(ALUSel), .MemRW(MemRW), .WBSel(WBSel), .CSRSel(CSRSel), .inst(INSTRUCTION), .BrEq(BrEq),
    .BrLt(BrLt));
  alu alu_1 (
    .Result({MEM_WRITE_ADDRESS[31:2], ALU_res}), .A(multiplexer_3_out), .B(multiplexer_4_out), .ALUSel(ALUSel));
  Multiplexer #(.enable("false"), .select(2), .width(32)) multiplexer_5 (
    .in0(mem_data), .in1({MEM_WRITE_ADDRESS[31:2], ALU_res}), .in2(adder_1_out), .out(multiplexer_5_out),
    .sel(WBSel));  // open: in3
  assign bit_extender_1_out = {{16{MEM_READ_DATA[15]}}, MEM_READ_DATA[15:0]};  // Bit_Extender bit_extender_1
  assign bit_extender_2_out = {{16{MEM_READ_DATA[31]}}, MEM_READ_DATA[31:16]};  // Bit_Extender bit_extender_2
  assign bit_extender_3_out = {{24{MEM_READ_DATA[7]}}, MEM_READ_DATA[7:0]};  // Bit_Extender bit_extender_3
  assign bit_extender_4_out = {{24{MEM_READ_DATA[15]}}, MEM_READ_DATA[15:8]};  // Bit_Extender bit_extender_4
  assign bit_extender_5_out = {{24{MEM_READ_DATA[23]}}, MEM_READ_DATA[23:16]};  // Bit_Extender bit_extender_5
  assign bit_extender_6_out = {{24{MEM_READ_DATA[31]}}, MEM_READ_DATA[31:24]};  // Bit_Extender bit_extender_6
  assign and_1_out = rs2 & 32'hffff;  // AND_Gate and_1, 32 bits wide
  Shifter #(.width(32)) shifter_1 (.in(rs2), .\dist (5'b10000), .out(shifter_1_out));
  Shifter #(.width(4)) shifter_2 (.in(4'b0001), .\dist (2'b01));  // open: out
  Shifter #(.width(4)) shifter_3 (.in(4'b0001), .\dist (2'b10));  // open: out
  Shifter #(.width(4)) shifter_4 (.in(4'b0001), .\dist (2'b11));  // open: out
  Shifter #(.shift("lr"), .width(4)) shifter_5 (.in(4'b1111), .\dist (2'b10), .out(shifter_5_out));
  Shifter #(.width(4)) shifter_6 (.in(4'b1111), .\dist (2'b10), .out(shifter_6_out));
  Multiplexer #(.enable("false"), .width(4)) multiplexer_6 (
    .in0(shifter_5_out), .in1(shifter_6_out), .out(multiplexer_6_out), .sel(ALU_res[1]));
  Multiplexer #(.enable("false"), .width(32)) multiplexer_7 (
    .in0(bit_extender_1_out), .in1(bit_extender_2_out), .out(multiplexer_7_out), .sel(ALU_res[1]));
  Multiplexer #(.enable("false"), .select(2), .width(32)) multiplexer_8 (
    .in0({{24{1'b0}}, rs2[7:0]}), .in1({{16{1'b0}}, rs2[7:0], {8{1'b0}}}),
    .in2({{8{1'b0}}, rs2[7:0], {16{1'b0}}}), .in3({rs2[7:0], {24{1'b0}}}), .out(multiplexer_8_out),
    .sel(ALU_res));
  Multiplexer #(.enable("false"), .width(32)) multiplexer_9 (
    .in0(and_1_out), .in1(shifter_1_out), .out(multiplexer_9_out), .sel(ALU_res[1]));
  Multiplexer #(.enable("false"), .select(2), .width(4)) multiplexer_10 (
    .in0(4'b0001), .out(multiplexer_10_out), .sel(ALU_res));  // open: in1, in2, in3
  Multiplexer #(.enable("false"), .select(2), .width(32)) multiplexer_11 (
    .in0(bit_extender_3_out), .in1(bit_extender_4_out), .in2(bit_extender_5_out), .in3(bit_extender_6_out),
    .out(multiplexer_11_out), .sel(ALU_res));
  Multiplexer #(.enable("false"), .select(2), .width(4)) multiplexer_12 (
    .in0(multiplexer_10_out), .in1(multiplexer_6_out), .in2(4'b1111), .out(multiplexer_12_out),
    .sel(INSTRUCTION[13:12]));  // open: in3
  Multiplexer #(.enable("false"), .select(2), .width(32)) multiplexer_13 (
    .in0(multiplexer_11_out), .in1(multiplexer_7_out), .in2(MEM_READ_DATA), .out(mem_data),
    .sel(INSTRUCTION[13:12]));  // open: in3
  Multiplexer #(.enable("false"), .select(2), .width(32)) multiplexer_14 (
    .in0(multiplexer_8_out), .in1(multiplexer_9_out), .in2(rs2), .out(MEM_WRITE_DATA),
    .sel(INSTRUCTION[13:12]));  // open: in3
  Multiplexer #(.enable("false"), .width(4)) multiplexer_15 (
    .in0(4'b0000), .in1(multiplexer_12_out), .out(MEM_WRITE_ENABLE), .sel(MemRW));

  assign MEM_WRITE_ADDRESS[1:0] = 2'b00;

  // Other names for the same wires on the sheet: mem_address_bit0 = ALU_res[0]; mem_address_bit1 = ALU_res[1];
  //   funt3[2:0] = INSTRUCTION[14:12]; ALU_res[31:2] = MEM_WRITE_ADDRESS[31:2]

  // Notes on the sheet:
  //   Output to IMEM
  //   IMEM (do **NOT** move this)
  //   Inputs from IMEM
  //   It is OK to move the PC, RegFile, ALU, MEM, Branch Comp, Imm Gen, and Control Logic to wherever is most convenient for you when constructing your CPU, and to delete this text
  //   Inputs/Outputs for testing. Do **NOT** move these.
  //   Outputs To DMEM
  //   DMEM (do **NOT** move this)
  //   Inputs From DMEM
  //   read data
  //   write data
endmodule
